// Logisim project ALU_32bit.circ as structural Verilog: 6 circuits, main circuit ALU_32bit
module ALU_32bit (
  input  [31:0] A,
  input  [31:0] B,
  input  Cin,
  output [31:0] Sum,
  output Cout
);

  wire n16bit_1_out_5;

  _16bit u_16bit_1 (.in_1(A[15:0]), .in_2(B[15:0]), .in_3(Cin), .out_4(Sum[15:0]), .out_5(n16bit_1_out_5));
  _16bit u_16bit_2 (.in_1(A[31:16]), .in_2(B[31:16]), .in_3(n16bit_1_out_5), .out_4(Sum[31:16]), .out_5(Cout));
endmodule

module _1bit (
  input  A,
  input  B,
  input  Cin,
  output S,
  output Cout
);

  wire nand_1_out, nand_2_out, xor_1_out;

  nand nand_1 (nand_1_out, A, B);
  nand nand_2 (nand_2_out, xor_1_out, Cin);
  xor xor_1 (xor_1_out, A, B);
  nand nand_3 (Cout, nand_1_out, nand_2_out);
  xor xor_2 (S, xor_1_out, Cin);
endmodule

module _2bit (
  input  [1:0] in_1,
  input  [1:0] in_2,
  input  in_3,
  output [1:0] out_4,
  output out_5
);

  wire \低_cout , \低_s , \高_s ;

  _1bit \u_高  (.A(in_1[1]), .B(in_2[1]), .Cin(\低_cout ), .S(\高_s ), .Cout(out_5));
  _1bit \u_低  (.A(in_1[0]), .B(in_2[0]), .Cin(in_3), .S(\低_s ), .Cout(\低_cout ));
  assign out_4 = {{1{\高_s }}, \低_s };  // Bit_Extender bit_extender_1
endmodule

module _4bit (
  input  [3:0] in_1,
  input  [3:0] in_2,
  input  in_3,
  output [3:0] out_4,
  output out_5
);

  wire n2bit_1_out_5;

  _2bit u_2bit_1 (.in_1(in_1[1:0]), .in_2(in_2[1:0]), .in_3(in_3), .out_4(out_4[1:0]), .out_5(n2bit_1_out_5));
  _2bit u_2bit_2 (.in_1(in_1[3:2]), .in_2(in_2[3:2]), .in_3(n2bit_1_out_5), .out_4(out_4[3:2]), .out_5(out_5));
endmodule

module _8bit (
  input  [7:0] in_1,
  input  [7:0] in_2,
  input  in_3,
  output [7:0] out_4,
  output out_5
);

  wire n4bit_1_out_5;

  _4bit u_4bit_1 (.in_1(in_1[3:0]), .in_2(in_2[3:0]), .in_3(in_3), .out_4(out_4[3:0]), .out_5(n4bit_1_out_5));
  _4bit u_4bit_2 (.in_1(in_1[7:4]), .in_2(in_2[7:4]), .in_3(n4bit_1_out_5), .out_4(out_4[7:4]), .out_5(out_5));
endmodule

module _16bit (
  input  [15:0] in_1,
  input  [15:0] in_2,
  input  in_3,
  output [15:0] out_4,
  output out_5
);

  wire n8bit_1_out_5;

  // Probe on in_1
  // Probe on in_2
  _8bit u_8bit_1 (.in_1(in_1[7:0]), .in_2(in_2[7:0]), .in_3(in_3), .out_4(out_4[7:0]), .out_5(n8bit_1_out_5));
  _8bit u_8bit_2 (.in_1(in_1[15:8]), .in_2(in_2[15:8]), .in_3(n8bit_1_out_5), .out_4(out_4[15:8]), .out_5(out_5));
  // Probe on out_4
endmodule
