// Logisim project P0_L2_nonexist_2023(1120-1149).circ as structural Verilog: 2 circuits, main circuit main
module main (
  input  [7:0] in_1,
  input  [7:0] in_2,
  input  [7:0] in_3,
  input  [7:0] in_4,
  input  [7:0] in_5,
  output [7:0] out_6
);

  wire bitfinder_1_found;
  wire [2:0] bitfinder_1_index;
  wire [7:0] bit_extender_1_out, check_1_out_2, check_2_out_2, check_3_out_2, check_4_out_2, check_5_out_2,
       or_1_out;

  check check_1 (.in_1(in_1), .out_2(check_1_out_2));
  check check_2 (.in_1(in_2), .out_2(check_2_out_2));
  check check_3 (.in_1(in_3), .out_2(check_3_out_2));
  check check_4 (.in_1(in_4), .out_2(check_4_out_2));
  check check_5 (.in_1(in_5), .out_2(check_5_out_2));
  assign or_1_out = check_1_out_2 | check_2_out_2 | check_3_out_2 | check_4_out_2 | check_5_out_2;  // OR_Gate or_1, 8 bits wide
  // Probe on or_1_out
  BitFinder #(.\type ("low0")) bitfinder_1 (.in(or_1_out), .index(bitfinder_1_index), .found(bitfinder_1_found));
  // Probe on bitfinder_1_found
  assign bit_extender_1_out = {{5{1'b0}}, bitfinder_1_index};  // Bit_Extender bit_extender_1
  Adder adder_1 (.a(bit_extender_1_out), .b(8'h1), .out(out_6));  // open: cin, cout
endmodule

module check (
  input  [7:0] in_1,
  output [7:0] out_2
);

  wire comparator_1_eq, comparator_2_eq, comparator_3_eq, comparator_4_eq, comparator_5_eq;
  wire [7:0] multiplexer_1_out, multiplexer_2_out, multiplexer_3_out, multiplexer_4_out, multiplexer_5_out;

  Comparator #(.mode("unsigned")) comparator_1 (.a(8'h1), .b(in_1), .eq(comparator_1_eq));  // open: gt, lt
  Comparator #(.mode("unsigned")) comparator_2 (.a(8'h2), .b(in_1), .eq(comparator_2_eq));  // open: gt, lt
  Comparator #(.mode("unsigned")) comparator_3 (.a(8'h3), .b(in_1), .eq(comparator_3_eq));  // open: gt, lt
  Comparator #(.mode("unsigned")) comparator_4 (.a(8'h4), .b(in_1), .eq(comparator_4_eq));  // open: gt, lt
  Comparator #(.mode("unsigned")) comparator_5 (.a(8'h5), .b(in_1), .eq(comparator_5_eq));  // open: gt, lt
  // Probe on 8'h10
  Multiplexer #(.width(8)) multiplexer_1 (
    .in0({8{1'b0}}), .in1(8'h1), .out(multiplexer_1_out), .sel(comparator_1_eq));  // open: en
  Multiplexer #(.width(8)) multiplexer_2 (
    .in0({8{1'b0}}), .in1(8'h2), .out(multiplexer_2_out), .sel(comparator_2_eq));  // open: en
  Multiplexer #(.width(8)) multiplexer_3 (
    .in0({8{1'b0}}), .in1(8'h4), .out(multiplexer_3_out), .sel(comparator_3_eq));  // open: en
  Multiplexer #(.width(8)) multiplexer_4 (
    .in0({8{1'b0}}), .in1(8'h8), .out(multiplexer_4_out), .sel(comparator_4_eq));  // open: en
  Multiplexer #(.width(8)) multiplexer_5 (
    .in0({8{1'b0}}), .in1(8'h10), .out(multiplexer_5_out), .sel(comparator_5_eq));  // open: en
  assign out_2 = multiplexer_1_out | multiplexer_2_out | multiplexer_3_out | multiplexer_4_out | multiplexer_5_out;  // OR_Gate or_1, 8 bits wide
endmodule
