// Logisim project P0_L2_nonexist_2023（改）.circ as structural Verilog: 2 circuits, main circuit main
module main (
  input  [7:0] in_1,
  input  [7:0] in_2,
  input  [7:0] in_3,
  input  [7:0] in_4,
  input  [7:0] in_5,
  output [7:0] out_6
);

  wire [2:0] bitfinder_1_index;
  wire [7:0] one_hot_1_out_2, one_hot_2_out_2, one_hot_3_out_2, one_hot_4_out_2, one_hot_5_out_2, or_1_out;

  one_hot one_hot_1 (.in_1(in_1), .out_2(one_hot_1_out_2));
  one_hot one_hot_2 (.in_1(in_2), .out_2(one_hot_2_out_2));
  one_hot one_hot_3 (.in_1(in_3), .out_2(one_hot_3_out_2));
  one_hot one_hot_4 (.in_1(in_4), .out_2(one_hot_4_out_2));
  one_hot one_hot_5 (.in_1(in_5), .out_2(one_hot_5_out_2));
  assign or_1_out = one_hot_1_out_2 | one_hot_2_out_2 | one_hot_3_out_2 | one_hot_4_out_2 | one_hot_5_out_2 | 8'h1;  // OR_Gate or_1, 8 bits wide
  BitFinder #(.\type ("low0")) bitfinder_1 (.in(or_1_out), .index(bitfinder_1_index));  // open: found
  assign out_6 = {{5{1'b0}}, bitfinder_1_index};  // Bit_Extender bit_extender_1
endmodule

module one_hot (
  input  [7:0] in_1,
  output [7:0] out_2
);

  wire [2:0] bit_extender_1_out;

  Bit_Extender #(.out_width(3)) bit_extender_1 (.in(in_1), .out(bit_extender_1_out));
  Shifter shifter_1 (.in(8'h1), .\dist (bit_extender_1_out), .out(out_2));
endmodule
