// Logisim project P0_L3_walker_2023(1120-1158).circ as structural Verilog: 2 circuits, main circuit main
module main (
  input  [1:0] in_1,
  input  in_2,
  input  in_3,
  output [3:0] out_4
);

  wire [2:0] next_logic_state_1_out_3, next_logic_state_2_out_3, register_1_q;
  wire [3:0] bit_extender_1_out;

  next_logic_state next_logic_state_1 (.in_1(in_1), .in_2(register_1_q), .out_3(next_logic_state_1_out_3));
  Register #(.width(3)) register_1 (
    .D(next_logic_state_1_out_3), .Q(register_1_q), .clk(in_3), .clr(in_2));  // open: en
  assign bit_extender_1_out = {{1{1'b0}}, next_logic_state_2_out_3};  // Bit_Extender bit_extender_1
  next_logic_state next_logic_state_2 (.in_1(in_1), .in_2(register_1_q), .out_3(next_logic_state_2_out_3));
  Adder #(.width(4)) adder_1 (.a(bit_extender_1_out), .b(4'b0001), .out(out_4));  // open: cin, cout

  // Other names for the same wires on the sheet: clk = in_3; in[1:0] = in_1; reset = in_2
endmodule

module next_logic_state (
  input  [1:0] in_1,
  input  [2:0] in_2,
  output [2:0] out_3
);

  wire and_1_out, and_2_out, and_3_out, and_4_out, and_5_out, and_6_out, and_7_out, and_8_out, and_9_out,
       and_10_out, and_11_out, and_12_out, and_13_out, and_14_out, and_15_out, and_16_out, and_17_out,
       and_18_out, and_19_out, and_20_out, and_21_out, and_22_out, and_23_out, and_24_out, and_25_out,
       and_26_out, and_27_out, and_28_out, and_29_out, and_30_out, and_31_out, and_32_out, and_33_out,
       and_34_out, and_35_out, and_36_out, and_37_out, and_38_out, and_39_out, and_40_out, and_41_out,
       and_42_out, and_43_out, and_44_out, and_45_out, and_46_out, and_47_out, and_48_out;

  and and_1 (and_1_out, ~in_2[2], ~in_2[1], ~in_2[0], ~in_1[1], in_1[0]);  // AND_Gate
  and and_2 (and_2_out, ~in_2[2], ~in_2[1], ~in_2[0], in_1[1], ~in_1[0]);  // AND_Gate
  and and_3 (and_3_out, ~in_2[2], ~in_2[1], in_2[0], in_1[1], ~in_1[0]);  // AND_Gate
  and and_4 (and_4_out, ~in_2[2], ~in_2[1], in_2[0], in_1[1], in_1[0]);  // AND_Gate
  and and_5 (and_5_out, ~in_2[2], in_2[1], ~in_2[0], ~in_1[1], ~in_1[0]);  // AND_Gate
  and and_6 (and_6_out, ~in_2[2], in_2[1], ~in_2[0], in_1[1], ~in_1[0]);  // AND_Gate
  and and_7 (and_7_out, ~in_2[2], in_2[1], in_2[0], ~in_1[1], ~in_1[0]);  // AND_Gate
  and and_8 (and_8_out, ~in_2[2], in_2[1], in_2[0], ~in_1[1], in_1[0]);  // AND_Gate
  and and_9 (and_9_out, in_2[2], ~in_2[1], ~in_2[0], ~in_1[1], ~in_1[0]);  // AND_Gate
  and and_10 (and_10_out, in_2[2], ~in_2[1], ~in_2[0], in_1[1], in_1[0]);  // AND_Gate
  and and_11 (and_11_out, in_2[2], ~in_2[1], in_2[0], in_1[1], ~in_1[0]);  // AND_Gate
  and and_12 (and_12_out, in_2[2], ~in_2[1], in_2[0], in_1[1], in_1[0]);  // AND_Gate
  and and_13 (and_13_out, in_2[2], in_2[1], ~in_2[0], ~in_1[1], in_1[0]);  // AND_Gate
  and and_14 (and_14_out, in_2[2], in_2[1], ~in_2[0], in_1[1], in_1[0]);  // AND_Gate
  and and_15 (and_15_out, in_2[2], in_2[1], in_2[0], ~in_1[1], ~in_1[0]);  // AND_Gate
  and and_16 (and_16_out, in_2[2], in_2[1], in_2[0], ~in_1[1], in_1[0]);  // AND_Gate
  or or_1 (out_3[0], and_1_out, and_2_out, and_3_out, and_4_out, and_5_out, and_6_out, and_7_out, and_8_out, and_9_out, and_10_out, and_11_out, and_12_out, and_13_out, and_14_out, and_15_out, and_16_out);
  and and_17 (and_17_out, ~in_2[2], ~in_2[1], ~in_2[0], in_1[1], ~in_1[0]);  // AND_Gate
  and and_18 (and_18_out, ~in_2[2], ~in_2[1], in_2[0], ~in_1[1], in_1[0]);  // AND_Gate
  and and_19 (and_19_out, ~in_2[2], in_2[1], ~in_2[0], ~in_1[1], in_1[0]);  // AND_Gate
  and and_20 (and_20_out, ~in_2[2], in_2[1], ~in_2[0], in_1[1], ~in_1[0]);  // AND_Gate
  and and_21 (and_21_out, ~in_2[2], in_2[1], ~in_2[0], in_1[1], in_1[0]);  // AND_Gate
  and and_22 (and_22_out, ~in_2[2], in_2[1], in_2[0], ~in_1[1], ~in_1[0]);  // AND_Gate
  and and_23 (and_23_out, ~in_2[2], in_2[1], in_2[0], ~in_1[1], in_1[0]);  // AND_Gate
  and and_24 (and_24_out, ~in_2[2], in_2[1], in_2[0], in_1[1], in_1[0]);  // AND_Gate
  and and_25 (and_25_out, in_2[2], ~in_2[1], ~in_2[0], in_1[1], in_1[0]);  // AND_Gate
  and and_26 (and_26_out, in_2[2], ~in_2[1], in_2[0], ~in_1[1], ~in_1[0]);  // AND_Gate
  and and_27 (and_27_out, in_2[2], in_2[1], ~in_2[0], ~in_1[1], ~in_1[0]);  // AND_Gate
  and and_28 (and_28_out, in_2[2], in_2[1], ~in_2[0], in_1[1], ~in_1[0]);  // AND_Gate
  and and_29 (and_29_out, in_2[2], in_2[1], ~in_2[0], in_1[1], in_1[0]);  // AND_Gate
  and and_30 (and_30_out, in_2[2], in_2[1], in_2[0], ~in_1[1], ~in_1[0]);  // AND_Gate
  and and_31 (and_31_out, in_2[2], in_2[1], in_2[0], ~in_1[1], in_1[0]);  // AND_Gate
  and and_32 (and_32_out, in_2[2], in_2[1], in_2[0], in_1[1], ~in_1[0]);  // AND_Gate
  or or_2 (out_3[1], and_17_out, and_18_out, and_19_out, and_20_out, and_21_out, and_22_out, and_23_out, and_24_out, and_25_out, and_26_out, and_27_out, and_28_out, and_29_out, and_30_out, and_31_out, and_32_out);
  and and_33 (and_33_out, ~in_2[2], ~in_2[1], ~in_2[0], in_1[1], ~in_1[0]);  // AND_Gate
  and and_34 (and_34_out, ~in_2[2], in_2[1], in_2[0], in_1[1], ~in_1[0]);  // AND_Gate
  and and_35 (and_35_out, in_2[2], ~in_2[1], ~in_2[0], ~in_1[1], ~in_1[0]);  // AND_Gate
  and and_36 (and_36_out, in_2[2], ~in_2[1], ~in_2[0], ~in_1[1], in_1[0]);  // AND_Gate
  and and_37 (and_37_out, in_2[2], ~in_2[1], ~in_2[0], in_1[1], ~in_1[0]);  // AND_Gate
  and and_38 (and_38_out, in_2[2], ~in_2[1], in_2[0], ~in_1[1], ~in_1[0]);  // AND_Gate
  and and_39 (and_39_out, in_2[2], ~in_2[1], in_2[0], ~in_1[1], in_1[0]);  // AND_Gate
  and and_40 (and_40_out, in_2[2], ~in_2[1], in_2[0], in_1[1], ~in_1[0]);  // AND_Gate
  and and_41 (and_41_out, in_2[2], ~in_2[1], in_2[0], in_1[1], in_1[0]);  // AND_Gate
  and and_42 (and_42_out, in_2[2], in_2[1], ~in_2[0], ~in_1[1], ~in_1[0]);  // AND_Gate
  and and_43 (and_43_out, in_2[2], in_2[1], ~in_2[0], ~in_1[1], in_1[0]);  // AND_Gate
  and and_44 (and_44_out, in_2[2], in_2[1], ~in_2[0], in_1[1], ~in_1[0]);  // AND_Gate
  and and_45 (and_45_out, in_2[2], in_2[1], ~in_2[0], in_1[1], in_1[0]);  // AND_Gate
  and and_46 (and_46_out, in_2[2], in_2[1], in_2[0], ~in_1[1], ~in_1[0]);  // AND_Gate
  and and_47 (and_47_out, in_2[2], in_2[1], in_2[0], ~in_1[1], in_1[0]);  // AND_Gate
  and and_48 (and_48_out, in_2[2], in_2[1], in_2[0], in_1[1], ~in_1[0]);  // AND_Gate
  or or_3 (out_3[2], and_33_out, and_34_out, and_35_out, and_36_out, and_37_out, and_38_out, and_39_out, and_40_out, and_41_out, and_42_out, and_43_out, and_44_out, and_45_out, and_46_out, and_47_out, and_48_out);

  // Other names for the same wires on the sheet: a0 = in_1[0]; a1 = in_1[1]; s0 = in_2[0]; s1 = in_2[1]; s2 = in_2[2];
  //   s0_prime = out_3[0]; s1_prime = out_3[1]; s2_prime = out_3[2]
endmodule
