// Logisim project P0_L3_walker_2023（改）.circ as structural Verilog: 3 circuits, main circuit main
module main (
  input  [1:0] in_1,
  input  in_2,
  input  in_3,
  output [3:0] out_4
);

  wire [2:0] next_state_logic_1_out_3, next_state_logic_2_out_3, register_1_q;
  wire [3:0] bit_extender_1_out;

  next_state_logic next_state_logic_1 (.in_1(register_1_q), .judge(in_1), .out_3(next_state_logic_1_out_3));
  Register #(.width(3)) register_1 (
    .D(next_state_logic_1_out_3), .Q(register_1_q), .clk(in_3), .clr(in_2));  // open: en
  next_state_logic next_state_logic_2 (.in_1(register_1_q), .judge(in_1), .out_3(next_state_logic_2_out_3));
  assign bit_extender_1_out = {{1{1'b0}}, next_state_logic_2_out_3};  // Bit_Extender bit_extender_1
  Adder #(.width(4)) adder_1 (.a(bit_extender_1_out), .b(4'b0001), .out(out_4));  // open: cin, cout

  // Other names for the same wires on the sheet: clk = in_3; in[1:0] = in_1; reset = in_2
endmodule

module judge (
  input  [2:0] in_1,
  input  [1:0] in_2,
  output [1:0] out_3
);

  wire and_1_out, and_2_out, and_3_out, and_4_out, and_5_out, and_6_out, and_7_out, and_8_out, and_9_out,
       and_10_out, and_11_out, and_12_out, not_1_out, not_2_out, not_3_out, not_4_out, not_5_out, not_6_out,
       not_7_out, not_8_out, not_9_out, not_10_out, not_11_out, not_12_out, not_13_out, not_14_out,
       not_15_out, not_16_out, not_17_out, not_18_out, not_19_out, not_20_out, not_21_out, not_22_out,
       not_23_out, not_24_out, not_25_out, not_26_out, not_27_out, not_28_out;

  not not_1 (not_1_out, in_1[2]);
  not not_2 (not_2_out, in_1[1]);
  not not_3 (not_3_out, in_1[0]);
  not not_4 (not_4_out, in_2[0]);
  not not_5 (not_5_out, in_1[2]);
  not not_6 (not_6_out, in_1[1]);
  not not_7 (not_7_out, in_2[1]);
  not not_8 (not_8_out, in_2[0]);
  not not_9 (not_9_out, in_1[2]);
  not not_10 (not_10_out, in_1[0]);
  not not_11 (not_11_out, in_2[1]);
  not not_12 (not_12_out, in_2[0]);
  not not_13 (not_13_out, in_1[2]);
  not not_14 (not_14_out, in_1[1]);
  not not_15 (not_15_out, in_1[0]);
  not not_16 (not_16_out, in_1[1]);
  not not_17 (not_17_out, in_2[1]);
  not not_18 (not_18_out, in_1[0]);
  not not_19 (not_19_out, in_2[1]);
  not not_20 (not_20_out, in_2[0]);
  not not_21 (not_21_out, in_1[2]);
  not not_22 (not_22_out, in_1[1]);
  not not_23 (not_23_out, in_2[1]);
  not not_24 (not_24_out, in_1[2]);
  not not_25 (not_25_out, in_2[0]);
  not not_26 (not_26_out, in_1[1]);
  not not_27 (not_27_out, in_2[1]);
  not not_28 (not_28_out, in_2[0]);
  and and_1 (and_1_out, not_1_out, not_2_out, not_3_out, in_2[1], not_4_out);
  and and_2 (and_2_out, not_5_out, not_6_out, in_1[0], not_7_out, not_8_out);
  and and_3 (and_3_out, not_9_out, in_1[1], not_10_out, not_11_out, not_12_out);
  and and_4 (and_4_out, not_13_out, in_1[1], in_1[0], in_2[1], in_2[0]);
  and and_5 (and_5_out, in_1[2], not_14_out, not_15_out, in_2[1], in_2[0]);
  and and_6 (and_6_out, in_1[2], not_16_out, in_1[0], not_17_out, in_2[0]);
  and and_7 (and_7_out, in_1[2], in_1[1], not_18_out, not_19_out, in_2[0]);
  and and_8 (and_8_out, in_1[2], in_1[1], in_1[0], in_2[1], not_20_out);
  and and_9 (and_9_out, not_21_out, not_22_out, not_23_out, in_2[0]);
  and and_10 (and_10_out, not_24_out, in_1[1], in_2[1], not_25_out);
  and and_11 (and_11_out, in_1[2], not_26_out, not_27_out, not_28_out);
  and and_12 (and_12_out, in_1[2], in_1[1], in_2[1], in_2[0]);
  or or_1 (out_3[1], and_1_out, and_2_out, and_3_out, and_4_out, and_5_out, and_6_out, and_7_out, and_8_out);
  or or_2 (out_3[0], and_9_out, and_10_out, and_11_out, and_12_out);
endmodule

module next_state_logic (
  input  [2:0] in_1,
  input  [1:0] judge,
  output [2:0] out_3
);

  wire [1:0] judge_1_out_3;
  wire [2:0] adder_1_out, subtractor_1_out;

  Adder #(.width(3)) adder_1 (.a(in_1), .b(3'b001), .out(adder_1_out));  // open: cin, cout
  Subtractor #(.width(3)) subtractor_1 (.a(in_1), .b(3'b001), .out(subtractor_1_out));  // open: bin, bout
  judge judge_1 (.in_1(in_1), .in_2(judge), .out_3(judge_1_out_3));
  Multiplexer #(.select(2), .width(3)) multiplexer_1 (
    .in0(in_1), .in1(adder_1_out), .in2(subtractor_1_out), .out(out_3), .sel(judge_1_out_3));  // open: in3, en
endmodule
