// Logisim project CRC.circ as structural Verilog: 3 circuits, main circuit CRC
module CRC (
  input  [7:0] in_1,
  input  [3:0] in_2,
  output [10:0] out_3
);

  wire [2:0] n4bit_div_1_out_3, n4bit_div_2_out_3, n4bit_div_3_out_3, n4bit_div_4_out_3, n4bit_div_5_out_3,
       n4bit_div_6_out_3, n4bit_div_7_out_3, n4bit_div_8_out_3;
  wire [3:0] bit_extender_2_out, next_1_out_4, next_2_out_4, next_3_out_4, next_4_out_4, next_5_out_4,
       next_6_out_4, next_7_out_4;
  wire [10:0] bit_extender_1_out, bit_extender_3_out, d, shifter_1_out;

  assign bit_extender_1_out = {{3{1'b0}}, in_1};  // Bit_Extender bit_extender_1
  Shifter #(.width(11), .shift("lr")) shifter_1 (.in(d), .\dist (4'b0111), .out(shifter_1_out));
  _4bit_div u_4bit_div_1 (.dividend(bit_extender_2_out), .divisor(in_2), .out_3(n4bit_div_1_out_3));  // open: out_4
  next next_1 (.in_1(d), .in_2(n4bit_div_1_out_3), .in_3(4'b0110), .out_4(next_1_out_4));
  next next_2 (.in_1(d), .in_2(n4bit_div_2_out_3), .in_3(4'b0010), .out_4(next_2_out_4));
  _4bit_div u_4bit_div_2 (.dividend(next_7_out_4), .divisor(in_2), .out_3(n4bit_div_2_out_3));  // open: out_4
  Shifter #(.width(11)) shifter_2 (.in(bit_extender_1_out), .\dist (4'b0011), .out(d));
  Bit_Extender #(.in_width(11), .out_width(4)) bit_extender_2 (.in(shifter_1_out), .out(bit_extender_2_out));
  _4bit_div u_4bit_div_3 (.dividend(next_1_out_4), .divisor(in_2), .out_3(n4bit_div_3_out_3));  // open: out_4
  _4bit_div u_4bit_div_4 (.dividend(next_2_out_4), .divisor(in_2), .out_3(n4bit_div_4_out_3));  // open: out_4
  next next_3 (.in_1(d), .in_2(n4bit_div_3_out_3), .in_3(4'b0101), .out_4(next_3_out_4));
  next next_4 (.in_1(d), .in_2(n4bit_div_4_out_3), .in_3(4'b0001), .out_4(next_4_out_4));
  next next_5 (.in_1(d), .in_2(n4bit_div_5_out_3), .in_3(4'b0100), .out_4(next_5_out_4));
  _4bit_div u_4bit_div_5 (.dividend(next_3_out_4), .divisor(in_2), .out_3(n4bit_div_5_out_3));  // open: out_4
  _4bit_div u_4bit_div_6 (.dividend(next_4_out_4), .divisor(in_2), .out_3(n4bit_div_6_out_3));  // open: out_4
  next next_6 (.in_1(d), .in_2(n4bit_div_6_out_3), .in_3(4'b0000), .out_4(next_6_out_4));
  _4bit_div u_4bit_div_7 (.dividend(next_5_out_4), .divisor(in_2), .out_3(n4bit_div_7_out_3));  // open: out_4
  _4bit_div u_4bit_div_8 (.dividend(next_6_out_4), .divisor(in_2), .out_3(n4bit_div_8_out_3));  // open: out_4
  next next_7 (.in_1(d), .in_2(n4bit_div_7_out_3), .in_3(4'b0011), .out_4(next_7_out_4));
  assign bit_extender_3_out = {{8{1'b0}}, n4bit_div_8_out_3};  // Bit_Extender bit_extender_3
  assign out_3 = bit_extender_3_out | d;  // OR_Gate or_1, 11 bits wide

  // Other names for the same wires on the sheet: dividend[10:0] = d; divisor[3:0] = in_2
endmodule

module _4bit_div (
  input  [3:0] dividend,
  input  [3:0] divisor,
  output [2:0] out_3,
  output out_4
);

  wire [3:0] multiplexer_1_out, xor_1_out;

  Multiplexer #(.width(4)) multiplexer_1 (
    .in0(dividend), .in1(xor_1_out), .out(multiplexer_1_out), .sel(dividend[3]));  // open: en
  assign xor_1_out = dividend ^ divisor;  // XOR_Gate xor_1, 4 bits wide
  Bit_Extender #(.in_width(4), .out_width(3)) bit_extender_1 (.in(multiplexer_1_out), .out(out_3));

  assign out_4 = dividend[3];

  // Other names for the same wires on the sheet: C[2:0] = out_3; D = dividend[3]
endmodule

module next (
  input  [10:0] in_1,
  input  [2:0] in_2,
  input  [3:0] in_3,
  output [3:0] out_4
);

  wire [3:0] bit_extender_1_out, bit_extender_2_out, shifter_2_out;
  wire [10:0] and_1_out, shifter_1_out;

  assign bit_extender_1_out = {{1{1'b0}}, in_2};  // Bit_Extender bit_extender_1
  Shifter #(.width(11), .shift("lr")) shifter_1 (.in(in_1), .\dist (in_3), .out(shifter_1_out));
  Shifter #(.width(4)) shifter_2 (.in(bit_extender_1_out), .\dist (2'b01), .out(shifter_2_out));
  Bit_Extender #(.in_width(11), .out_width(4)) bit_extender_2 (.in(and_1_out), .out(bit_extender_2_out));
  assign and_1_out = shifter_1_out & 11'h1;  // AND_Gate and_1, 11 bits wide
  assign out_4 = shifter_2_out | bit_extender_2_out;  // OR_Gate or_1, 4 bits wide

  // Other names for the same wires on the sheet: A[10:0] = in_1; bit[3:0] = in_3; div[2:0] = in_2
endmodule
