// Logisim project fsm.circ as structural Verilog: 3 circuits, main circuit fsm
module fsm (
  input  in_1,
  input  [1:0] in_2,
  output Z
);

  wire clk;
  wire [1:0] multiplexer_1_out, next_state_logic_1_s_prime, register_1_q;

  next_state_logic next_state_logic_1 (.S(register_1_q), .In(in_2), .S_prime(next_state_logic_1_s_prime));
  Register #(.width(2)) register_1 (.D(multiplexer_1_out), .Q(register_1_q), .clk(clk));  // open: en, clr
  Multiplexer #(.width(2)) multiplexer_1 (
    .in0(next_state_logic_1_s_prime), .in1(2'b00), .out(multiplexer_1_out), .sel(in_1));  // open: en
  Clock clock_1 (.out(clk));
  output_logic output_logic_1 (.S(register_1_q), .In(in_2), .Z(Z));

  // Other names for the same wires on the sheet: In[1:0] = in_2
endmodule

module next_state_logic (
  input  [1:0] S,
  input  [1:0] In,
  output [1:0] S_prime
);

  wire and_1_out, and_2_out, and_3_out, and_4_out, and_5_out, and_6_out, and_7_out, and_8_out, ni0, ni1, ns0,
       ns1;

  not not_1 (ns0, S[0]);
  not not_2 (ns1, S[1]);
  not not_3 (ni0, In[0]);
  not not_4 (ni1, In[1]);
  and and_1 (and_1_out, ni1, S[0], ns1);
  and and_2 (and_2_out, ni0, S[0], ns1);
  and and_3 (and_3_out, ni1, S[1], ns0);
  and and_4 (and_4_out, ni0, S[1], ns0);
  and and_5 (and_5_out, ni1, In[0], ns1, ns0);
  and and_6 (and_6_out, ni1, In[0], S[1], S[0]);
  and and_7 (and_7_out, ni0, S[0], ns1);
  and and_8 (and_8_out, ni0, S[1], ns0);
  or or_1 (S_prime[1], and_1_out, and_2_out, and_3_out, and_4_out);
  or or_2 (S_prime[0], and_5_out, and_6_out, and_7_out, and_8_out);

  // Other names for the same wires on the sheet: i0 = In[0]; i1 = In[1]; s0_prime = S_prime[0]; s1_prime = S_prime[1]
endmodule

module output_logic (
  input  [1:0] S,
  input  [1:0] In,
  output Z
);

  wire not_1_out;

  not not_1 (not_1_out, In[0]);
  and and_1 (Z, S[0], S[1], not_1_out);
endmodule
