// Logisim project ftoi.circ as structural Verilog: 1 circuit, main circuit ftoi
module ftoi (
  input  [15:0] in_1,
  output [31:0] out_2
);

  wire all_zero, multiplexer_1_out, multiplexer_2_out, neg, out_zero, s;
  wire [4:0] controlled_buffer_1_out, E, exp, nE, subtractor_2_out;
  wire [9:0] frac;
  wire [15:0] shifter_3_out, shifter_4_out;
  wire [31:0] _1, _2, bit_extender_1_out, bit_extender_2_out, bit_extender_4_out, multiplexer_3_out,
       multiplexer_4_out, negator_1_out, shifter_1_out, shifter_2_out, shifter_5_out, shifter_6_out;

  Comparator #(.width(5), .mode("unsigned")) comparator_1 (.a(exp), .b({5{1'b1}}), .eq(out_zero));  // open: gt, lt
  Multiplexer multiplexer_1 (.in0(1'b1), .in1(1'b0), .out(multiplexer_1_out), .sel(all_zero));  // open: en
  Multiplexer multiplexer_2 (.in0(1'b1), .in1(1'b0), .out(multiplexer_2_out), .sel(all_zero));  // open: en
  Multiplexer #(.width(32)) multiplexer_3 (.in0(_2), .in1(_1), .out(multiplexer_3_out), .sel(neg));  // open: en
  assign bit_extender_1_out = {{31{1'b0}}, multiplexer_1_out};  // Bit_Extender bit_extender_1
  Shifter #(.width(32)) shifter_1 (.in(bit_extender_1_out), .\dist (E), .out(shifter_1_out));
  assign bit_extender_2_out = {{31{1'b0}}, multiplexer_2_out};  // Bit_Extender bit_extender_2
  Shifter #(.width(32), .shift("lr")) shifter_2 (.in(bit_extender_2_out), .\dist (nE), .out(shifter_2_out));
  Multiplexer #(.width(32)) multiplexer_4 (
    .in0(multiplexer_3_out), .in1(negator_1_out), .out(multiplexer_4_out), .sel(s));  // open: en
  Negator #(.width(32)) negator_1 (.in(multiplexer_3_out), .out(negator_1_out));
  Shifter #(.width(16), .shift("lr")) shifter_3 (.in(in_1), .\dist (4'b1111), .out(shifter_3_out));
  Bit_Extender #(.in_width(16), .out_width(1)) bit_extender_3 (.in(shifter_3_out), .out(s));
  Comparator #(.width(5), .mode("unsigned")) comparator_2 (.a(exp), .b({5{1'b0}}), .eq(all_zero));  // open: gt, lt
  Multiplexer #(.width(32)) multiplexer_5 (.in0(shifter_1_out), .in1(shifter_2_out), .out(_1), .sel(neg));  // open: en
  Multiplexer #(.width(32)) multiplexer_6 (
    .in0(multiplexer_4_out), .in1({32{1'b0}}), .out(out_2), .sel(out_zero));  // open: en
  Shifter #(.width(16), .shift("lr")) shifter_4 (.in(in_1), .\dist (4'b1010), .out(shifter_4_out));
  Subtractor #(.width(5)) subtractor_1 (.a(exp), .b(5'b01111), .out(E), .bout(neg));  // open: bin
  assign bit_extender_4_out = {{22{1'b0}}, frac};  // Bit_Extender bit_extender_4
  Bit_Extender #(.in_width(16), .out_width(5)) bit_extender_5 (.in(shifter_4_out), .out(exp));
  assign controlled_buffer_1_out = neg ? E : 5'bz;  // Controlled_Buffer controlled_buffer_1
  Shifter #(.width(32)) shifter_5 (.in(bit_extender_4_out), .\dist (5'b00101), .out(shifter_5_out));
  Shifter #(.width(32), .shift("lr")) shifter_6 (.in(shifter_5_out), .\dist (subtractor_2_out), .out(shifter_6_out));
  Subtractor #(.width(5)) subtractor_2 (.a(5'b01111), .b(E), .out(subtractor_2_out));  // open: bin, bout
  Bit_Extender #(.in_width(16), .out_width(10)) bit_extender_6 (.in(in_1), .out(frac));
  Negator #(.width(5)) negator_2 (.in(controlled_buffer_1_out), .out(nE));
  assign _2 = _1 | shifter_6_out;  // OR_Gate or_1, 32 bits wide

  // Other names for the same wires on the sheet: float[15:0] = in_1; out[31:0] = out_2
endmodule
