// Logisim project navigation.circ as structural Verilog: 3 circuits, main circuit navigation
module navigation (
  input  [1:0] in_1,
  input  in_2,
  input  in_3,
  output out_4,
  output out_5
);

  wire next_state_logic_1_hit;
  wire [2:0] next_state_logic_1_s_prime, register_1_q;

  next_state_logic next_state_logic_1 (
    .dir(in_1), .s(register_1_q), .hit(next_state_logic_1_hit), .s_prime(next_state_logic_1_s_prime));
  Register #(.width(3)) register_1 (
    .D(next_state_logic_1_s_prime), .Q(register_1_q), .clk(in_2), .clr(in_3));  // open: en
  Register #(.width(1)) register_2 (.D(next_state_logic_1_hit), .Q(out_5), .clk(in_2), .clr(in_3));  // open: en
  // Probe on out_4
  output_logic output_logic_1 (.s(register_1_q), .arrive(out_4));
  // Probe on register_1_q

  // Other names for the same wires on the sheet: arrive = out_4; clk = in_2; dir[1:0] = in_1; hit = out_5;
  //   reset = in_3
endmodule

module next_state_logic (
  input  [1:0] dir,
  input  [2:0] s,
  output hit,
  output [2:0] s_prime
);

  wire and_1_out, and_2_out, and_3_out, and_4_out, and_5_out, and_6_out, and_7_out, and_8_out, and_9_out,
       and_10_out, and_11_out, and_12_out, and_14_out, and_15_out, and_16_out, and_17_out, and_18_out, nd0,
       nd1, ns0, ns1, ns2, or_3_out, or_4_out;

  not not_1 (nd0, dir[0]);
  not not_2 (nd1, dir[1]);
  not not_3 (ns0, s[0]);
  not not_4 (ns1, s[1]);
  not not_5 (ns2, s[2]);
  and and_1 (and_1_out, ns0, ns2, dir[1], nd0);
  and and_2 (and_2_out, ns0, ns2, nd1, dir[0]);
  and and_3 (and_3_out, ns2, s[0], dir[0], dir[1]);
  and and_4 (and_4_out, ns1, ns2, dir[1], dir[0]);
  and and_5 (and_5_out, s[1], s[0], ns2, nd1, nd0);
  or or_1 (hit, and_1_out, and_2_out, and_3_out, and_4_out, and_5_out);
  and and_6 (and_6_out, ns2, s[1], ns0, nd1, nd0);
  and and_7 (and_7_out, ns2, s[1], s[0], nd1, dir[0]);
  and and_8 (and_8_out, ns1, s[0], nd1);
  and and_9 (and_9_out, s[1], ns0, nd1, dir[0]);
  and and_10 (and_10_out, s[1], ns0, dir[1], nd0);
  and and_11 (and_11_out, s[1], s[0], dir[1], dir[0]);
  and and_12 (and_12_out, s[1], s[0], nd1, nd0);
  or or_2 (s_prime[2], and_6_out, and_7_out);
  or or_3 (or_3_out, and_8_out, and_9_out, and_10_out, and_11_out, and_12_out);
  and and_13 (s_prime[1], or_3_out, ns2);
  and and_14 (and_14_out, ns1, nd1, nd0);
  and and_15 (and_15_out, s[0], nd1, nd0);
  and and_16 (and_16_out, s[1], dir[1], dir[0]);
  and and_17 (and_17_out, s[0], dir[1], dir[0]);
  and and_18 (and_18_out, s[1], s[0], dir[1]);
  or or_4 (or_4_out, and_14_out, and_15_out, and_16_out, and_17_out, and_18_out);
  and and_19 (s_prime[0], or_4_out, ns2);

  // Other names for the same wires on the sheet: d0 = dir[0]; d1 = dir[1]; s0_prime = s_prime[0];
  //   s1_prime = s_prime[1]; s2_prime = s_prime[2]
endmodule

module output_logic (
  input  [2:0] s,
  output arrive
);

  wire not_1_out, not_2_out;

  not not_1 (not_1_out, s[0]);
  not not_2 (not_2_out, s[1]);
  and and_1 (arrive, not_1_out, not_2_out, s[2]);
endmodule
