// Logisim project cpu.circ as structural Verilog: 8 circuits, main circuit main
module GRF (
  input  in_1,
  input  in_2,
  input  in_3,
  input  [4:0] in_4,
  input  [4:0] in_5,
  input  [4:0] in_6,
  input  [31:0] in_7,
  output [31:0] out_8,
  output [31:0] out_9
);

  wire [31:0] i0, i1, i2, i3, i4, i5, i6, i7, i8, i9, i10, i11, i12, i13, i14, i15, i16, i17, i18, i19, i20,
       i21, i22, i23, i24, i25, i26, i27, i28, i29, i30, i31, o0, o1, o2, o3, o4, o5, o6, o7, o8, o9, o10,
       o11, o12, o13, o14, o15, o16, o17, o18, o19, o20, o21, o22, o23, o24, o25, o26, o27, o28, o29, o30,
       o31;

  Demultiplexer #(.select(5), .width(32), .tristate("true")) demultiplexer_1 (
    .out0(i0), .out1(i1), .out2(i2), .out3(i3), .out4(i4), .out5(i5), .out6(i6), .out7(i7), .out8(i8),
    .out9(i9), .out10(i10), .out11(i11), .out12(i12), .out13(i13), .out14(i14), .out15(i15), .out16(i16),
    .out17(i17), .out18(i18), .out19(i19), .out20(i20), .out21(i21), .out22(i22), .out23(i23), .out24(i24),
    .out25(i25), .out26(i26), .out27(i27), .out28(i28), .out29(i29), .out30(i30), .out31(i31), .in(in_7),
    .sel(in_6), .en(in_3));
  Register #(.width(32)) register_1 (.D(i0), .en(in_3), .Q(o0), .clk(in_1), .clr(1'b1));
  Register #(.width(32)) register_2 (.D(i8), .en(in_3), .Q(o8), .clk(in_1), .clr(in_2));
  Register #(.width(32)) register_3 (.D(i16), .en(in_3), .Q(o16), .clk(in_1), .clr(in_2));
  Register #(.width(32)) register_4 (.D(i24), .en(in_3), .Q(o24), .clk(in_1), .clr(in_2));
  Register #(.width(32)) register_5 (.D(i1), .en(in_3), .Q(o1), .clk(in_1), .clr(in_2));
  Register #(.width(32)) register_6 (.D(i9), .en(in_3), .Q(o9), .clk(in_1), .clr(in_2));
  Register #(.width(32)) register_7 (.D(i17), .en(in_3), .Q(o17), .clk(in_1), .clr(in_2));
  Register #(.width(32)) register_8 (.D(i25), .en(in_3), .Q(o25), .clk(in_1), .clr(in_2));
  Multiplexer #(.select(5), .width(32)) multiplexer_1 (
    .in0(o0), .in1(o1), .in2(o2), .in3(o3), .in4(o4), .in5(o5), .in6(o6), .in7(o7), .in8(o8), .in9(o9),
    .in10(o10), .in11(o11), .in12(o12), .in13(o13), .in14(o14), .in15(o15), .in16(o16), .in17(o17),
    .in18(o18), .in19(o19), .in20(o20), .in21(o21), .in22(o22), .in23(o23), .in24(o24), .in25(o25),
    .in26(o26), .in27(o27), .in28(o28), .in29(o29), .in30(o30), .in31(o31), .out(out_8), .sel(in_4));  // open: en
  Register #(.width(32)) register_9 (.D(i2), .en(in_3), .Q(o2), .clk(in_1), .clr(in_2));
  Register #(.width(32)) register_10 (.D(i10), .en(in_3), .Q(o10), .clk(in_1), .clr(in_2));
  Register #(.width(32)) register_11 (.D(i18), .en(in_3), .Q(o18), .clk(in_1), .clr(in_2));
  Register #(.width(32)) register_12 (.D(i26), .en(in_3), .Q(o26), .clk(in_1), .clr(in_2));
  Register #(.width(32)) register_13 (.D(i3), .en(in_3), .Q(o3), .clk(in_1), .clr(in_2));
  Register #(.width(32)) register_14 (.D(i11), .en(in_3), .Q(o11), .clk(in_1), .clr(in_2));
  Register #(.width(32)) register_15 (.D(i19), .en(in_3), .Q(o19), .clk(in_1), .clr(in_2));
  Register #(.width(32)) register_16 (.D(i27), .en(in_3), .Q(o27), .clk(in_1), .clr(in_2));
  Multiplexer #(.select(5), .width(32)) multiplexer_2 (
    .in0(o0), .in1(o1), .in2(o2), .in3(o3), .in4(o4), .in5(o5), .in6(o6), .in7(o7), .in8(o8), .in9(o9),
    .in10(o10), .in11(o11), .in12(o12), .in13(o13), .in14(o14), .in15(o15), .in16(o16), .in17(o17),
    .in18(o18), .in19(o19), .in20(o20), .in21(o21), .in22(o22), .in23(o23), .in24(o24), .in25(o25),
    .in26(o26), .in27(o27), .in28(o28), .in29(o29), .in30(o30), .in31(o31), .out(out_9), .sel(in_5));  // open: en
  Register #(.width(32)) register_17 (.D(i4), .en(in_3), .Q(o4), .clk(in_1), .clr(in_2));
  Register #(.width(32)) register_18 (.D(i12), .en(in_3), .Q(o12), .clk(in_1), .clr(in_2));
  Register #(.width(32)) register_19 (.D(i20), .en(in_3), .Q(o20), .clk(in_1), .clr(in_2));
  Register #(.width(32)) register_20 (.D(i28), .en(in_3), .Q(o28), .clk(in_1), .clr(in_2));
  Register #(.width(32)) register_21 (.D(i5), .en(in_3), .Q(o5), .clk(in_1), .clr(in_2));
  Register #(.width(32)) register_22 (.D(i13), .en(in_3), .Q(o13), .clk(in_1), .clr(in_2));
  Register #(.width(32)) register_23 (.D(i21), .en(in_3), .Q(o21), .clk(in_1), .clr(in_2));
  Register #(.width(32)) register_24 (.D(i29), .en(in_3), .Q(o29), .clk(in_1), .clr(in_2));
  Register #(.width(32)) register_25 (.D(i6), .en(in_3), .Q(o6), .clk(in_1), .clr(in_2));
  Register #(.width(32)) register_26 (.D(i14), .en(in_3), .Q(o14), .clk(in_1), .clr(in_2));
  Register #(.width(32)) register_27 (.D(i22), .en(in_3), .Q(o22), .clk(in_1), .clr(in_2));
  Register #(.width(32)) register_28 (.D(i30), .en(in_3), .Q(o30), .clk(in_1), .clr(in_2));
  Register #(.width(32)) register_29 (.D(i7), .en(in_3), .Q(o7), .clk(in_1), .clr(in_2));
  Register #(.width(32)) register_30 (.D(i15), .en(in_3), .Q(o15), .clk(in_1), .clr(in_2));
  Register #(.width(32)) register_31 (.D(i23), .en(in_3), .Q(o23), .clk(in_1), .clr(in_2));
  Register #(.width(32)) register_32 (.D(i31), .en(in_3), .Q(o31), .clk(in_1), .clr(in_2));

  // Other names for the same wires on the sheet: A1[4:0] = in_4; A2[4:0] = in_5; A3[4:0] = in_6; clk = in_1;
  //   RD1[31:0] = out_8; RD2[31:0] = out_9; reset = in_2; WD[31:0] = in_7; WE = in_3
endmodule

module main (
  input  in_1,
  output [31:0] Instr,
  output [31:0] pc,
  output RegWrite,
  output [4:0] RegAddr,
  output [31:0] RegData,
  output MemWrite,
  output [31:0] MemAddr,
  output [31:0] MemData
);

  wire ALUSrc, Branch, clk, equal, Jr, Jump, LinkRa, MemtoReg, RegDst, SignExtend;
  wire [2:0] ALUop, BranchOp;
  wire [4:0] multiplexer_1_out;
  wire [31:0] dm_1_out_6, ext_1_out_3, grf_1_out_8, multiplexer_4_out, multiplexer_5_out, PC_4;

  Clock clock_1 (.out(clk));
  // Probe on pc
  Multiplexer #(.width(5)) multiplexer_1 (
    .in0(Instr[15:11]), .in1(Instr[20:16]), .out(multiplexer_1_out), .sel(RegDst));  // open: en
  IFU ifu_1 (
    .in_3(in_1), .in_4(clk), .in_5(ext_1_out_3), .out_9(pc), .out_10(Instr), .in_6(Branch), .in_1(Jump),
    .in_2(Jr), .in_7(Instr[25:0]), .in_8(grf_1_out_8), .out_11(PC_4));
  Multiplexer #(.width(5)) multiplexer_2 (
    .in0(multiplexer_1_out), .in1({5{1'b1}}), .out(RegAddr), .sel(LinkRa));  // open: en
  Multiplexer #(.width(32)) multiplexer_3 (
    .in0(multiplexer_5_out), .in1(PC_4), .out(RegData), .sel(LinkRa));  // open: en
  GRF grf_1 (
    .in_1(clk), .in_2(in_1), .in_3(RegWrite), .in_4(Instr[25:21]), .in_5(Instr[20:16]), .in_6(RegAddr),
    .in_7(RegData), .out_8(grf_1_out_8), .out_9(MemData));
  EXT ext_1 (.in_1(Instr[15:0]), .in_2(SignExtend), .out_3(ext_1_out_3));
  // Probe on ext_1_out_3
  Multiplexer #(.width(32)) multiplexer_4 (
    .in0(MemData), .in1(ext_1_out_3), .out(multiplexer_4_out), .sel(ALUSrc));  // open: en
  Controller controller_1 (
    .in_1(Instr[31:26]), .in_2(Instr[5:0]), .out_3(RegDst), .out_4(Jump), .out_5(LinkRa), .out_8(MemtoReg),
    .out_6(Jr), .out_9(RegWrite), .out_10(MemWrite), .out_7(BranchOp), .out_11(SignExtend), .out_12(ALUSrc),
    .out_13(ALUop));
  ALU alu_1 (
    .in_1(grf_1_out_8), .in_2(multiplexer_4_out), .in_3(Instr[10:6]), .in_4(ALUop), .out_5(MemAddr),
    .out_6(equal));
  // Probe on ALUop
  CheckBranch checkbranch_1 (.in_1(BranchOp), .in_2(equal), .in_3(grf_1_out_8), .in_4(Instr[20:16]), .out_5(Branch));
  Multiplexer #(.width(32)) multiplexer_5 (
    .in0(MemAddr), .in1(dm_1_out_6), .out(multiplexer_5_out), .sel(MemtoReg));  // open: en
  DM dm_1 (.in_4(MemAddr[13:2]), .in_5(MemData), .out_6(dm_1_out_6), .in_1(MemWrite), .in_2(clk), .in_3(in_1));
  // Probe on Instr
  // Probe on RegData
  // Probe on MemData

  // Other names for the same wires on the sheet: funct[5:0] = Instr[5:0]; imm16_offset[15:0] = Instr[15:0];
  //   shamt[4:0] = Instr[10:6]; rd[4:0] = Instr[15:11]; rt[4:0] = Instr[20:16]; rs[4:0] = Instr[25:21];
  //   op[5:0] = Instr[31:26]; reset = in_1
endmodule

module IFU (
  input  in_1,
  input  in_2,
  input  in_3,
  input  in_4,
  input  [31:0] in_5,
  input  in_6,
  input  [25:0] in_7,
  input  [31:0] in_8,
  output [31:0] out_9,
  output [31:0] out_10,
  output [31:0] out_11
);

  wire comparator_1_eq;
  wire [31:0] adder_1_out, multiplexer_1_out, multiplexer_3_out, NextPC, register_1_q, shifter_1_out,
       subtractor_1_out;

  Register #(.width(32)) register_1 (.D(NextPC), .Q(register_1_q), .clk(in_4), .clr(in_3));  // open: en
  // Probe on adder_1_out
  Shifter #(.width(32)) shifter_1 (.in(in_5), .\dist (5'b00010), .out(shifter_1_out));
  Comparator #(.width(32), .mode("unsigned")) comparator_1 (
    .a(register_1_q), .b({32{1'b0}}), .eq(comparator_1_eq));  // open: gt, lt
  Multiplexer #(.width(32)) multiplexer_1 (
    .in0(out_11), .in1(adder_1_out), .out(multiplexer_1_out), .sel(in_6));  // open: en
  Adder #(.width(32)) adder_1 (.a(out_11), .b(shifter_1_out), .out(adder_1_out));  // open: cin, cout
  Multiplexer #(.width(32)) multiplexer_2 (
    .in0(register_1_q), .in1(32'h3000), .out(out_9), .sel(comparator_1_eq));  // open: en
  Multiplexer #(.width(32)) multiplexer_3 (
    .in0(multiplexer_1_out), .in1({out_9[31:28], in_7, 2'b00}), .out(multiplexer_3_out), .sel(in_1));  // open: en
  // Probe on subtractor_1_out
  Subtractor #(.width(32)) subtractor_1 (.a(out_9), .b(32'h3000), .out(subtractor_1_out));  // open: bin, bout
  Multiplexer #(.width(32)) multiplexer_4 (.in0(multiplexer_3_out), .in1(in_8), .out(NextPC), .sel(in_2));  // open: en
  Adder #(.width(32)) adder_2 (.a(out_9), .b(32'h4), .out(out_11));  // open: cin, cout
  ROM #(.addrWidth(12), .dataWidth(32)) rom_1 (.addr(subtractor_1_out[13:2]), .data(out_10));  // open: sel

  // Other names for the same wires on the sheet: Instr26[25:0] = in_7; PC[31:0] = out_9; branch = in_6; clk = in_4;
  //   Instr[31:0] = out_10; j_jal = in_1; jr = in_2; Offset[31:0] = in_5; PC_4[31:0] = out_11; ra[31:0] = in_8;
  //   reset = in_3

  // Notes on the sheet:
  //   PC
  //   contents of rom_1 (hex, n*v repeats v):
  //   3401d238 3c01ff98 3402ee5a 3c02f39c 3403a874 3c03670e 34048463 3c0467d9 34054816 3c056f69 3406065a
  //   3c062538 340785b4 3c07f211 3408fdbc 3c08f040 3409e383 3c09f5ca 340a9258 3c0afd86 340b5a5c 3c0bff2c
  //   340c8255 3c0c0720 340d6818 3c0d6e2c 340eb8be 3c0ef520 340fc856 3c0ffbe8 3410b238 3c10f985 341133fc
  //   3c11f4df 34129640 3c121e76 34136f46 3c13ff40 3414cd20 3c14f9e3 34159252 3c1573db 3416825b 3c164dc0
  //   34174d65 3c17fdde 34181106 3c181120 3419592c 3c195812 341a39d0 3c1a59b8 341b8272 3c1bf814 341c6652
  //   3c1c1488 341d9f80 3c1d6b81 341ea6c5 3c1ef727 341f6ac9 3c1f2494 4ad022 0 34190010 af2e0004 2d39022
  //   34120060 8e46ffc0 34040030 8c8bfff4 0 36fbc7ca 340d0028 8da50008 3c1f788d 3991822 d2b820 4e9820
  //   3408003c ad13ffe8 34100054 ae080008 3c0c2aed 0 34080038 8d0f0004 34160054 8ec60000 0 120d0071
  //   136a00b2 10e20049 13bb008e 341d1768 34111768 3c1d3afa 3c113afa 13b100f4 35d727bc 36ff5b40 2895822
  //   15d020 146d022 3c091410 34140000 8e9e0000 3c15fa22 34150038 aebb0010 35d59318 0 369934d8 0 340c0028
  //   ad810018 35757780 341c0000 8f850000 0 a2c820 340b0020 8d670020 34150000 8ea50000 12a5006e 13fd008f
  //   1086ffe3 13ff0025 341a2064 34072064 3c1af890 3c07f890 13470020 6a9820 34000048 8c0e0000 31e822
  //   3599f7d0 37c8020 3c12f6c4 127e020 32f0022 3c02fc18 35d67e3f 3c050d2a 3618fd42 37a45700 296d822
  //   24fe820 341a0018 af47fff8 afa822 1535820 35826bb1 34090008 ad24fff8 1374ffe8 136d0100 1014004c
  //   11310092 341abfd4 3409bfd4 3c1a01ee 3c0901ee 13490068 375d3264 34020010 ac48fff0 34060030 acdcffe4
  //   2108020 34080048 8d14002c 14de820 34140020 ae870000 1c9a020 341c0040 8f970008 3407005c 8cf40010
  //   34070038 ace4fff0 35b8c97b 34070048 8ce10048 373a55c4 3410004c 8e030024 4*0 364a2962 12a7ff9f
  //   12feff9e 10df006d 13ceffdf 341850c6 340850c6 3c18beef 3c08beef 130800d3 3e7a022 0 3428d1c1 3c0141d0
  //   370820c0 3c1d4b58 1731022 3929020 34090040 8d250000 16ff022 3414005c ae87005c 3c0df872 3727799a 0 0
  //   340f0008 8dea0000 0 3b7c020 2b63020 1e35020 10fe0008 10de004e 13d40095 101bffe5 340e913e 340a913e
  //   3c0e52e4 3c0a52e4 11ca00b3 341f004c affaffdc 3c110d44 34150028 aea9ffdc 34000010 8c120000 3b86822
  //   1ca8020 3c1cfb94 1f71820 867822 3c1af9ae 337e022 341c004c 8f87ffc0 481822 26e2022 2d53822 34150000
  //   aea90000 3c014e36 37a4f77c 0 3a4f020 113cffa0 1033ff9f 13a3004f 1014ff7d 340e9308 340d9308 3c0ea205
  //   3c0da205 11cdffbe 3780f923 34100020 8e0affe0 35b211bb 0 34110064 8e260060 24b2820 34170000 8ee70000
  //   34020058 ac5effc4 3c1affc0 34805e58 3403004c ac78002c 0 340f0060 8de2004c 2db6022 3c137636 0 159e022
  //   32cf820 34180038 8f04001c 340d004c 8db00020 1050ffc1 12d9002b 1100004e 133f0005 341c9e26 341e9e26
  //   3c1c8be8 3c1e8be8 139e0048 c53022 2148020 34180028 af120020 3c18fbdd 367ad204 3699752c 31fb020
  //   340b005c 8d680058 1b9f020 341b0004 af670000 23a8020 3c1bf80d 34020058 ac41002c 341a0010 af4e0008
  //   2b18022 340d001c ada70000 1980822 34bca7e8 0 341e001c 8fdcfff4 139e0050 1305ff36 101e002a 110fffbc
  //   340437ae 341037ae 3c046468 3c106468 1090ff2f 3be4020 3c1d35b0 34000058 ac170000 2b19022 340c0010
  //   ad8bfffc 3c1ef244 34130008 ae790000 0 1a68022 34070010 acea0004 34150048 8eb50038 360ebe88 7df820
  //   341c004c 8f9b0014 3638399c 3d69820 341e000c afc0fff4 3c03f32a 2d3e822 3530f6f6 1177ffc0 1083feef
  //   1266ffe2 13c0feed 34189f3c 341b9f3c 3c187f42 3c1b7f42 131b0024 340b0060 ad72004c 3403005c ac7a0034
  //   340d0028 ada20014 340d0000 8dbd0000 0 3c31822 0 37debc57 3c02f78f 2f56822 2329022 3eb820 3735e2d0
  //   34080054 8d0affbc 35ec60a4 340e0008 8dcb0004 34170050 8ee60020 3c0cf4e8 284f020 308d822 1149ff9c
  //   12fdff0e 12bcfeca 11b0ff0c 34092ec7 34102ec7 3c096c44 3c106c44 1130ff94 1000fe60
endmodule

module EXT (
  input  [15:0] in_1,
  input  in_2,
  output [31:0] out_3
);

  wire [31:0] bit_extender_1_out, bit_extender_2_out;

  assign bit_extender_1_out = {{16{1'b0}}, in_1};  // Bit_Extender bit_extender_1
  assign bit_extender_2_out = {{16{in_1[15]}}, in_1};  // Bit_Extender bit_extender_2
  Multiplexer #(.width(32)) multiplexer_1 (
    .in0(bit_extender_1_out), .in1(bit_extender_2_out), .out(out_3), .sel(in_2));  // open: en

  // Other names for the same wires on the sheet: extOp = in_2; imm16[15:0] = in_1; imm32[31:0] = out_3
endmodule

module ALU (
  input  [31:0] in_1,
  input  [31:0] in_2,
  input  [4:0] in_3,
  input  [2:0] in_4,
  output [31:0] out_5,
  output out_6
);

  wire [31:0] adder_1_out, and_1_out, or_1_out, shifter_1_out, subtractor_1_out;

  Comparator #(.width(32), .mode("unsigned")) comparator_1 (.a(in_1), .b(in_2), .eq(out_6));  // open: gt, lt
  Adder #(.width(32)) adder_1 (.a(in_1), .b(in_2), .out(adder_1_out));  // open: cin, cout
  Subtractor #(.width(32)) subtractor_1 (.a(in_1), .b(in_2), .out(subtractor_1_out));  // open: bin, bout
  assign and_1_out = in_1 & in_2;  // AND_Gate and_1, 32 bits wide
  assign or_1_out = in_1 | in_2;  // OR_Gate or_1, 32 bits wide
  Shifter #(.width(32)) shifter_1 (.in(in_2), .\dist (in_3), .out(shifter_1_out));
  Multiplexer #(.select(3), .width(32)) multiplexer_1 (
    .in0(adder_1_out), .in1(subtractor_1_out), .in2(and_1_out), .in3(or_1_out), .in4(shifter_1_out),
    .in5({in_2[15:0], {16{1'b0}}}), .out(out_5), .sel(in_4));  // open: in6, in7, en

  // Other names for the same wires on the sheet: SrcB[31:0] = in_2; ALUop[2:0] = in_4; equal = out_6;
  //   result[31:0] = out_5; shamt[4:0] = in_3; SrcA[31:0] = in_1
endmodule

module Controller (
  input  [5:0] in_1,
  input  [5:0] in_2,
  output out_3,
  output out_4,
  output out_5,
  output out_6,
  output [2:0] out_7,
  output out_8,
  output out_9,
  output out_10,
  output out_11,
  output out_12,
  output [2:0] out_13
);

  wire addu, beq, bgez_bltz, bgtz, blez, bne, j, lui, not_1_out, not_2_out, not_3_out, not_4_out, not_5_out,
       not_6_out, not_7_out, not_8_out, not_9_out, not_10_out, not_11_out, not_12_out, ori, R, sll, subu, sw;

  and _000000 (R, not_3_out, not_1_out, not_2_out, not_6_out, not_5_out, not_4_out);
  and _001101 (ori, not_3_out, not_1_out, in_1[3], in_1[2], not_5_out, in_1[0]);
  and _100011 (out_8, in_1[5], not_1_out, not_2_out, not_6_out, in_1[1], in_1[0]);
  and _101011 (sw, in_1[5], not_1_out, in_1[3], not_6_out, in_1[1], in_1[0]);
  and _000100 (beq, not_3_out, not_1_out, not_2_out, in_1[2], not_5_out, not_4_out);
  and _001111 (lui, not_3_out, not_1_out, in_1[3], in_1[2], in_1[1], in_1[0]);
  and _000010 (j, not_3_out, not_1_out, not_2_out, not_6_out, in_1[1], not_4_out);
  and _000011 (out_5, not_3_out, not_1_out, not_2_out, not_6_out, in_1[1], in_1[0]);
  and _000111 (bgtz, not_3_out, not_1_out, not_2_out, in_1[2], in_1[1], in_1[0]);
  and _000110 (blez, not_3_out, not_1_out, not_2_out, in_1[2], in_1[1], not_4_out);
  and _000001 (bgez_bltz, not_3_out, not_1_out, not_2_out, not_6_out, not_5_out, in_1[0]);
  and _000101 (bne, not_3_out, not_1_out, not_2_out, in_1[2], not_5_out, in_1[0]);
  not not_1 (not_1_out, in_1[4]);
  not not_2 (not_2_out, in_1[3]);
  not not_3 (not_3_out, in_1[5]);
  not not_4 (not_4_out, in_1[0]);
  not not_5 (not_5_out, in_1[1]);
  not not_6 (not_6_out, in_1[2]);
  not not_7 (not_7_out, in_2[5]);
  not not_8 (not_8_out, in_2[4]);
  not not_9 (not_9_out, in_2[1]);
  not not_10 (not_10_out, in_2[3]);
  not not_11 (not_11_out, in_2[0]);
  not not_12 (not_12_out, in_2[2]);
  and _100000 (addu, in_2[5], not_8_out, not_10_out, R, not_12_out, not_9_out, not_11_out);
  and _100010 (subu, in_2[5], not_8_out, not_10_out, R, not_12_out, in_2[1], not_11_out);
  and _000000_2 (sll, not_7_out, not_8_out, not_10_out, R, not_12_out, not_9_out, not_11_out);
  and _001000 (out_6, not_7_out, not_8_out, in_2[3], R, not_12_out, not_9_out, not_11_out);
  not not_13 (out_3, R);
  or or_1 (out_4, j, out_5);
  or or_2 (out_9, addu, subu, sll, out_8, out_5, ori, lui);
  buf or_3 (out_10, sw);  // OR_Gate
  or or_4 (out_7[0], bgez_bltz, beq, blez);
  or or_5 (out_7[1], bgtz, blez);
  or or_6 (out_7[2], bne, beq);
  or or_7 (out_11, out_8, sw, beq);
  or or_8 (out_12, out_8, sw, ori, lui);
  or or_9 (out_13[0], subu, ori, lui, beq);
  buf or_10 (out_13[1], ori);  // OR_Gate
  or or_11 (out_13[2], lui, sll);

  // Other names for the same wires on the sheet: ALUop[2:0] = out_13; ALUSrc = out_12; BranchOp[2:0] = out_7;
  //   funct[5:0] = in_2; jal = out_5; LinkRa = out_5; Jr = out_6; Jump = out_4; lw = out_8; MemtoReg = out_8;
  //   MemWrite = out_10; op[5:0] = in_1; RegDst = out_3; RegWrite = out_9; SignExtend = out_11

  // Notes on the sheet:
  //   beq no need
  //   which reg to write
  //   give imm to SrcB
endmodule

module DM (
  input  in_1,
  input  in_2,
  input  in_3,
  input  [11:0] in_4,
  input  [31:0] in_5,
  output [31:0] out_6
);

  RAM #(.addrWidth(12), .dataWidth(32), .bus("separate")) ram_1 (
    .addr(in_4), .din(in_5), .data(out_6), .str(in_1), .clk(in_2), .clr(in_3));  // open: sel, ld

  // Other names for the same wires on the sheet: clk = in_2; MemAddr[11:0] = in_4; MemData[31:0] = in_5;
  //   MenWrite = in_1; ReadData[31:0] = out_6; reset = in_3
endmodule

module CheckBranch (
  input  [2:0] in_1,
  input  in_2,
  input  [31:0] in_3,
  input  [4:0] in_4,
  output out_5
);

  wire comparator_1_gt, comparator_1_lt, comparator_2_eq, multiplexer_1_out, not_1_out, not_2_out, not_3_out;

  Comparator #(.width(32)) comparator_1 (
    .a(in_3), .b({32{1'b0}}), .gt(comparator_1_gt), .lt(comparator_1_lt));  // open: eq
  not not_1 (not_1_out, comparator_1_gt);
  not not_2 (not_2_out, comparator_1_lt);
  Comparator #(.width(5), .mode("unsigned")) comparator_2 (
    .a(in_4), .b(5'b00001), .eq(comparator_2_eq));  // open: gt, lt
  Multiplexer multiplexer_1 (
    .in0(comparator_1_lt), .in1(not_2_out), .out(multiplexer_1_out), .sel(comparator_2_eq));  // open: en
  not not_3 (not_3_out, in_2);
  Multiplexer #(.select(3)) multiplexer_2 (
    .in0(1'b0), .in1(multiplexer_1_out), .in2(comparator_1_gt), .in3(not_1_out), .in4(not_3_out), .in5(in_2),
    .out(out_5), .sel(in_1));  // open: in6, in7, en

  // Other names for the same wires on the sheet: Branch = out_5; BranchOp[2:0] = in_1; equal = in_2; exOP[4:0] = in_4;
  //   rs[31:0] = in_3
endmodule
